# Fritzing sketch C86_Circuit (saved by Fritzing 0.9.0b)
breadboards: 1

parts:
  R4 = Resistor [tolerance=±5% resistance=4.7k package=THT]  # not connected
  R5 = Resistor [tolerance=±5% resistance=4.7k package=THT]
  C3 = Ceramic Capacitor [capacitance=100nF package="100 mil [THT, multilayer]"]
  R6 = Resistor [tolerance=±5% resistance=1k package=THT]
  C4 = Ceramic Capacitor [capacitance=47nF package="100 mil [THT, multilayer]"]
  パーツ4 = Audio Jack Breakout
  パーツ6 = Arduino Mega ADK (Rev3)
  IC2 = IC, DIP package, 28 pins [chip_label="AquesTalk ATP3011F4"]
  パーツ8 = Barometric Pressure Sensor - BMP085 Breakout
  パーツ9 = Barometric Pressure Sensor - BMP085 Breakout

nets:
  N1: R5.Pin_0, パーツ6.D20/SDA, IC2.pin27, パーツ9.GND
  5V: C3.0, パーツ6.5V, IC2.pin7, IC2.pin20, パーツ8.VCC
  GND: C3.1, C4.0, パーツ4.GND, パーツ6.GND, IC2.pin4, IC2.pin8, IC2.pin22, パーツ8.GND, パーツ9.XCLR
  N2: R6.Pin_0, IC2.pin12
  N3: R6.Pin_1, C4.1, パーツ4.TIP
  N4: パーツ6.D21/SCL, IC2.pin28, パーツ9.EOC
  N5: パーツ6.D17/RX2, パーツ8.EOC
  N6: パーツ6.D16/TX2, パーツ8.XCLR
  N7: パーツ6.RESET, IC2.pin1
  N8: パーツ6.3V3, パーツ9.SCL
  N9: パーツ8.SCL, パーツ8.SDA

custom parts:
  Barometric Pressure Sensor - BMP085 Breakout: Description: This is a simple breakout board for the BMP085 high-precision, low-power barometric pressure sensor. The BMP085 offers a measuring range of 300 to 1100 hPa with an absolute accuracy of down to 0.03 hPa. It's based on piezo-resistive technology for EMC robustness, high accuracy and linearity as well as long term stability. This sensor supports a voltage supply between 1.8 and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
  Barometric Pressure Sensor - BMP085 Breakout: Description: This is a simple breakout board for the BMP085 high-precision, low-power barometric pressure sensor. The BMP085 offers a measuring range of 300 to 1100 hPa with an absolute accuracy of down to 0.03 hPa. It's based on piezo-resistive technology for EMC robustness, high accuracy and linearity as well as long term stability. This sensor supports a voltage supply between 1.8 and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
